# Fritzing sketch hydroponics_schematic (saved by Fritzing 0.9.3b)
breadboards: 1

parts:
  Part2 = Adafruit AS7341
  DHT1 = DHT22 Humidity and Temperature Sensor
  Part3 = Arduino Uno (Rev3)
  KY-1 = Relay [package=THT]  # not connected
  KY-2 = Relay [package=THT]  # not connected
  KY-3 = Relay [package=THT]  # not connected
  F1 = Fan - Ventilador [package=THT]  # not connected
  S2 = PH meter [package=THT]  # not connected
  Raspberry_Pi_1 = Raspberry Pi 4 [part_number=RPI-4-b]  # not connected
  U1 = Vibration Motor- ROB-08449 [package=vibe-motor-10mm]  # not connected
  hc-sr1 = hc-sr04

nets:
  VCC: Part2.VCC, DHT1.VDD, Part3.5V
  GND: Part2.GND, DHT1.GND, Part3.GND, hc-sr1.GND
  N1: Part2.SCL, Part3.A5/SCL
  N2: Part2.SDA, Part3.A4/SDA
  N3: DHT1.DATA, Part3.D4
  N4: Part3.D8, hc-sr1.Trig
  N5: Part3.D9_PWM, hc-sr1.Echo

notes:
  pH Meter PH-4502C
  V-----------
  GND------
  GND
  Po---------
  Do
  To
  Water atomizer
  Digital (Yellow)
  5V (Red)
  GND (Black)
  Grow lights
  5V (Red)
  GND (Black)
  TDS sensor
  GND
  VCC
  A
  DHT22 temperature & humidity
  Fan 5V
  Water pump
  Air pump
  Color sensor AS7341
  Ultrasonic distance sensor

custom parts:
  Relay: The Keyes 5V relay module is suitable for SCM development, home appliance control. It uses a 5V~12V TIL control signal which can control DC / AC signal.
  Fan - Ventilador: Ventilador de 2 pines, se encuentra comunmente en computadoras de escritorio
  Raspberry Pi 4: The RPi4, a faster version of the awesome Raspberry Pi 2 B ARM Board with 40 pin gpio. Ready for special Raspberry Pi B+ and RPi2 Hat (Hardware attached (on) top)
